// Logisim project Project4Given.circ as structural Verilog: 16 circuits, main circuit main
module main (
  input  [3:0] in_1,
  input  [3:0] in_2,
  input  [3:0] in_3,
  input  [3:0] in_4,
  input  [3:0] in_5
);

  wire CLK, keyboard_1_avail, keyboard_2_avail, keyboarddriver_1_read, keyboarddriver_2_read,
       pull_resistor_1_node, ttydriver_1_write, ttydriver_2_write, ttydriver_3_write, vpwbmonitor_1_last_fe;
  wire [3:0] vpwbmonitor_1_last_addr;
  wire [6:0] keyboard_1_data, keyboard_2_data, ttydriver_1_data, ttydriver_2_data, ttydriver_3_data;
  wire [7:0] vpwbmonitor_1_last_data;
  wire [24:0] vpwbmonitor_1_out_4;
  wire [31:0] vpwbmonitor_1_out_3;

  Clock clock_1 (.out(CLK));
  Keyboard keyboard_1 (
    .clk(CLK), .re(keyboarddriver_1_read), .avail(keyboard_1_avail), .data(keyboard_1_data));  // open: clr
  Keyboard keyboard_2 (
    .clk(CLK), .re(keyboarddriver_2_read), .avail(keyboard_2_avail), .data(keyboard_2_data));  // open: clr
  Pull_Resistor #(.pull(1)) pull_resistor_1 (.node(pull_resistor_1_node));
  KeyboardDriver keyboarddriver_1 (
    .DATA(keyboard_1_data), .DEST(in_1), .DR(keyboard_1_avail), .CLK(CLK), .RXIN(pull_resistor_1_node),
    .READ(keyboarddriver_1_read), .TXOUT(pull_resistor_1_node));
  KeyboardDriver keyboarddriver_2 (
    .DATA(keyboard_2_data), .DEST(in_3), .DR(keyboard_2_avail), .CLK(CLK), .RXIN(pull_resistor_1_node),
    .READ(keyboarddriver_2_read), .TXOUT(pull_resistor_1_node));
  // Probe on vpwbmonitor_1_out_3
  VPWBMonitor vpwbmonitor_1 (
    .RXIN(pull_resistor_1_node), .CLK(CLK), .LAST_FE(vpwbmonitor_1_last_fe),
    .LAST_ADDR(vpwbmonitor_1_last_addr), .LAST_DATA(vpwbmonitor_1_last_data), .out_3(vpwbmonitor_1_out_3),
    .out_4(vpwbmonitor_1_out_4));
  TTY tty_1 (.data(ttydriver_1_data), .clk(CLK), .we(ttydriver_1_write));  // open: clr
  TTYDriver ttydriver_1 (
    .RXIN(pull_resistor_1_node), .CLK(CLK), .TTY_ADDR(in_2), .TXOUT(pull_resistor_1_node),
    .WRITE(ttydriver_1_write), .DATA(ttydriver_1_data));
  TTY tty_2 (.data(ttydriver_2_data), .clk(CLK), .we(ttydriver_2_write));  // open: clr
  TTYDriver ttydriver_2 (
    .RXIN(pull_resistor_1_node), .CLK(CLK), .TTY_ADDR(in_4), .TXOUT(pull_resistor_1_node),
    .WRITE(ttydriver_2_write), .DATA(ttydriver_2_data));
  TTY tty_3 (.data(ttydriver_3_data), .clk(CLK), .we(ttydriver_3_write));  // open: clr
  TTYDriver ttydriver_3 (
    .RXIN(pull_resistor_1_node), .CLK(CLK), .TTY_ADDR(in_5), .TXOUT(pull_resistor_1_node),
    .WRITE(ttydriver_3_write), .DATA(ttydriver_3_data));
  // Probe on vpwbmonitor_1_out_4
  // Probe on vpwbmonitor_1_last_fe
  // Probe on vpwbmonitor_1_last_addr
  // Probe on vpwbmonitor_1_last_data
endmodule

module KeyboardDriver (
  input  DR,
  input  [6:0] DATA,
  input  RXIN,
  input  [3:0] DEST,
  input  CLK,
  output TXOUT,
  output READ
);

  wire ADDR, and_1_out, CHKDR, CS, JUMP, O, or_1_out, txrxd_1_din, vpwbcontroller_1_ser_out, W;
  wire [5:5] rom_1_data;
  wire [7:0] NPC, PC, PCPLUS1, PCTARGET;
  wire [11:0] multiplexer_1_out;

  Register register_1 (.D(NPC), .en(1'b1), .clk(CLK), .Q(PC));  // open: clr
  Adder adder_1 (.a(8'h1), .b(PC), .out(PCPLUS1));  // open: cin, cout
  ROM #(.dataWidth(16)) rom_1 (.addr(PC), .data({PCTARGET, JUMP, CHKDR, rom_1_data[5], READ, ADDR, O, W, CS}));
  Multiplexer #(.width(12)) multiplexer_1 (.in0(12'h1), .in1({DEST, 1'b0, DATA}), .out(multiplexer_1_out), .sel(ADDR));
  VPWBController vpwbcontroller_1 (
    .O(O), .ADDR(ADDR), .DATAIN(multiplexer_1_out), .CS(CS), .W(W), .CLK(CLK), .SER_IN(txrxd_1_din),
    .SER_OUT(vpwbcontroller_1_ser_out));  // open: I, DATAOUT
  and and_1 (and_1_out, CHKDR, DR);
  or or_1 (or_1_out, and_1_out, JUMP);
  Multiplexer #(.width(8)) multiplexer_2 (.in0(PCPLUS1), .in1(PCTARGET), .out(NPC), .sel(or_1_out));
  TXRXD txrxd_1 (.DOUT(vpwbcontroller_1_ser_out), .RXIN(RXIN), .DIN(txrxd_1_din), .TXOUT(TXOUT));

  // Other names for the same wires on the sheet: DATA_t[6:0] = DATA

  // Notes on the sheet:
  //   contents of rom_1 (hex, n*v repeats v):
  //   7 4 7 547 387 1c 387
endmodule

module TTYDriver (
  input  RXIN,
  input  [3:0] TTY_ADDR,
  input  CLK,
  output [6:0] DATA,
  output TXOUT,
  output WRITE
);

  wire ADDR, and_1_out, CHKDR, comparator_1_eq, CS, DR, JUMP, not_1_out, O, or_1_out, txrxd_1_din,
       vpwbcontroller_1_ser_out, W, WRITE_TTY;
  wire [5:5] rom_1_data;
  wire [7:0] NPC, PC, PCPLUS1, PCTARGET;
  wire [11:0] DATAOUT, register_2_q;

  Register register_1 (.D(NPC), .en(1'b1), .clk(CLK), .Q(PC));  // open: clr
  Adder adder_1 (.a(8'h1), .b(PC), .out(PCPLUS1));  // open: cin, cout
  ROM #(.dataWidth(16)) rom_1 (.addr(PC), .data({PCTARGET, JUMP, CHKDR, rom_1_data[5], WRITE_TTY, ADDR, O, W, CS}));
  Register #(.width(12)) register_2 (
    .D(DATAOUT), .en(not_1_out), .clk(CLK), .Q({register_2_q[11:2], DR, register_2_q[0]}));  // open: clr
  not not_1 (not_1_out, O);
  and and_1 (and_1_out, CHKDR, DR);
  VPWBController vpwbcontroller_1 (
    .O(O), .ADDR(ADDR), .DATAIN({4'b1111, TTY_ADDR, 4'b0001}), .CS(CS), .W(W), .CLK(CLK),
    .SER_IN(txrxd_1_din), .DATAOUT(DATAOUT), .SER_OUT(vpwbcontroller_1_ser_out));  // open: I
  Multiplexer #(.width(8)) multiplexer_1 (.in0(PCPLUS1), .in1(PCTARGET), .out(NPC), .sel(or_1_out));
  or or_1 (or_1_out, and_1_out, JUMP);
  Comparator #(.mode("unsigned"), .width(4)) comparator_1 (
    .a(register_2_q[11:8]), .b(TTY_ADDR), .eq(comparator_1_eq));  // open: gt, lt
  and and_2 (WRITE, comparator_1_eq, WRITE_TTY);
  Multiplexer #(.width(7)) multiplexer_2 (
    .in0({7{1'b0}}), .in1({register_2_q[6:2], DR, register_2_q[0]}), .out(DATA), .sel(WRITE));
  TXRXD txrxd_1 (.DOUT(vpwbcontroller_1_ser_out), .RXIN(RXIN), .DIN(txrxd_1_din), .TXOUT(TXOUT));

  // Other names for the same wires on the sheet: CHAR[6:0] = DATA

  // Notes on the sheet:
  //   contents of rom_1 (hex, n*v repeats v):
  //   7 4 7 2 647 87 a 17 87
endmodule

module VPWBMonitor (
  input  RXIN,
  input  CLK,
  output [31:0] out_3,
  output [24:0] out_4,
  output LAST_FE,
  output [3:0] LAST_ADDR,
  output [7:0] LAST_DATA
);

  wire B0_ERR, B1_ERR, B2_ERR, B3_ERR, B4_ERR, B5_ERR, B6_ERR, B7_ERR, B8_ERR, B9_ERR, BA_ERR, BB_ERR,
       FOUND_IDLE, I4, I5, I6, I7, I8, I9, I10, I11, I12, I13, I14, I15, I16, I17, I18, I19, I20, I21, I22,
       I23, I24, I25, I26, I27, I28, I29, NEW_IDLE, not_7_out;
  wire [0:0] not_1_out, not_2_out, not_9_out, not_10_out, not_15_out, not_16_out, shifter_1_out_3,
       shifter_2_out_3, shifter_3_out_3, shifter_6_out_3, shifter_7_out_3, shifter_8_out_3, shifter_10_out_3,
       shifter_11_out_3, shifter_12_out_3;
  wire [1:0] shifter_1_out, shifter_2_out, shifter_3_out, shifter_6_out, shifter_7_out, shifter_8_out,
       shifter_10_out, shifter_11_out, shifter_12_out;
  wire [4:0] FRAME_LENGTH, priority_encoder_1_out;
  wire [5:0] subtractor_1_out, subtractor_2_out;
  wire [9:0] shifter_12_out_2;
  wire [10:0] shifter_11_out_2;
  wire [11:0] shifter_10_out_2, shifter_13_out;
  wire [13:0] shifter_8_out_2;
  wire [14:0] shifter_7_out_2;
  wire [15:0] shifter_6_out_2, shifter_9_out;
  wire [17:0] shifter_3_out_2;
  wire [18:0] shifter_2_out_2;
  wire [19:0] shifter_1_out_2, shifter_4_out;
  wire [24:0] and_6_out, not_8_out;
  wire [25:0] shifter_5_out;

  not not_1 (not_1_out[0], LAST_DATA[1]);
  not not_2 (not_2_out[0], LAST_DATA[3]);
  Subtractor #(.width(6)) subtractor_1 (
    .a(6'b011001), .b({1'b0, FRAME_LENGTH}), .out(subtractor_1_out));  // open: bin, bout
  Shifter #(.shift("lr"), .width(23)) shifter_1 (
    .in(out_4[24:2]), .\dist ({4'b0000, LAST_DATA[0]}),
    .out({shifter_1_out_2, shifter_1_out, shifter_1_out_3[0]}));
  Shifter #(.shift("lr"), .width(22)) shifter_2 (
    .in({shifter_1_out_2, shifter_1_out}), .\dist ({4'b0000, not_1_out[0]}),
    .out({shifter_2_out_2, shifter_2_out, shifter_2_out_3[0]}));
  Shifter #(.shift("lr"), .width(21)) shifter_3 (
    .in({shifter_2_out_2, shifter_2_out}), .\dist ({4'b0000, LAST_DATA[2]}),
    .out({shifter_3_out_2, shifter_3_out, shifter_3_out_3[0]}));
  Shifter #(.shift("lr"), .width(20)) shifter_4 (
    .in({shifter_3_out_2, shifter_3_out}), .\dist ({4'b0000, not_2_out[0]}), .out(shifter_4_out));
  // Probe on shifter_5_out
  and and_1 (B0_ERR, ~out_4[1], ~out_4[2], ~out_4[3]);  // AND_Gate
  not not_3 (LAST_DATA[0], out_4[2]);
  and and_2 (B1_ERR, shifter_1_out_3[0], shifter_1_out[0], shifter_1_out[1]);
  not not_4 (LAST_DATA[1], shifter_1_out[0]);
  and and_3 (B2_ERR, ~shifter_2_out_3[0], ~shifter_2_out[0], ~shifter_2_out[1]);  // AND_Gate
  not not_5 (LAST_DATA[2], shifter_2_out[0]);
  and and_4 (B3_ERR, shifter_3_out_3[0], shifter_3_out[0], shifter_3_out[1]);
  not not_6 (LAST_DATA[3], shifter_3_out[0]);
  not not_7 (not_7_out, RXIN);
  Shift_Register #(.length(32)) shift_register_1 (
    .shift(1'b1), .in(not_7_out), .clk(CLK), .out(out_3[31]), .q0(out_3[0]), .q1(out_3[1]), .q2(out_3[2]),
    .q3(out_3[3]), .q4(out_3[4]), .q5(out_3[5]), .q6(out_3[6]), .q7(out_3[7]), .q8(out_3[8]), .q9(out_3[9]),
    .q10(out_3[10]), .q11(out_3[11]), .q12(out_3[12]), .q13(out_3[13]), .q14(out_3[14]), .q15(out_3[15]),
    .q16(out_3[16]), .q17(out_3[17]), .q18(out_3[18]), .q19(out_3[19]), .q20(out_3[20]), .q21(out_3[21]),
    .q22(out_3[22]), .q23(out_3[23]), .q24(out_3[24]), .q25(out_3[25]), .q26(out_3[26]), .q27(out_3[27]),
    .q28(out_3[28]), .q29(out_3[29]), .q30(out_3[30]));  // open: load, clr, d0, d1, d2, d3, d4, d5, d6, d7, d8, d9, d10, d11, d12, d13, d14, d15, d16, d17, d18, d19, d20, d21, d22, d23, d24, d25, d26, d27, d28, d29, d30, d31, q31
  and and_5 (NEW_IDLE, ~out_3[0], ~out_3[1], ~out_3[2], out_3[3]);  // AND_Gate
  assign not_8_out = ~shifter_5_out[24:0];  // NOT_Gate not_8, 25 bits wide
  Shifter #(.shift("ar"), .width(26)) shifter_5 (.in(26'h2000000), .\dist (subtractor_1_out[4:0]), .out(shifter_5_out));
  not not_9 (not_9_out[0], LAST_DATA[5]);
  not not_10 (not_10_out[0], LAST_DATA[7]);
  Shifter #(.shift("lr"), .width(19)) shifter_6 (
    .in(shifter_4_out[19:1]), .\dist ({4'b0000, LAST_DATA[4]}),
    .out({shifter_6_out_2, shifter_6_out, shifter_6_out_3[0]}));
  Shifter #(.shift("lr"), .width(18)) shifter_7 (
    .in({shifter_6_out_2, shifter_6_out}), .\dist ({4'b0000, not_9_out[0]}),
    .out({shifter_7_out_2, shifter_7_out, shifter_7_out_3[0]}));
  Shifter #(.shift("lr"), .width(17)) shifter_8 (
    .in({shifter_7_out_2, shifter_7_out}), .\dist ({4'b0000, LAST_DATA[6]}),
    .out({shifter_8_out_2, shifter_8_out, shifter_8_out_3[0]}));
  Shifter #(.shift("lr"), .width(16)) shifter_9 (
    .in({shifter_8_out_2, shifter_8_out}), .\dist ({3'b000, not_10_out[0]}), .out(shifter_9_out));
  // Probe on and_6_out
  Register #(.width(25)) register_1 (.D(and_6_out), .en(NEW_IDLE), .clk(CLK), .Q(out_4));  // open: clr
  assign and_6_out = out_3[27:3] & not_8_out;  // AND_Gate and_6, 25 bits wide
  and and_7 (B4_ERR, ~shifter_4_out[0], ~shifter_4_out[1], ~shifter_4_out[2]);  // AND_Gate
  not not_11 (LAST_DATA[4], shifter_4_out[1]);
  and and_8 (B5_ERR, shifter_6_out_3[0], shifter_6_out[0], shifter_6_out[1]);
  not not_12 (LAST_DATA[5], shifter_6_out[0]);
  and and_9 (B6_ERR, ~shifter_7_out_3[0], ~shifter_7_out[0], ~shifter_7_out[1]);  // AND_Gate
  not not_13 (LAST_DATA[6], shifter_7_out[0]);
  and and_10 (B7_ERR, shifter_8_out_3[0], shifter_8_out[0], shifter_8_out[1]);
  not not_14 (LAST_DATA[7], shifter_8_out[0]);
  not not_15 (not_15_out[0], LAST_ADDR[1]);
  not not_16 (not_16_out[0], LAST_ADDR[3]);
  and and_11 (B8_ERR, ~shifter_9_out[0], ~shifter_9_out[1], ~shifter_9_out[2]);  // AND_Gate
  not not_17 (LAST_ADDR[0], shifter_9_out[1]);
  Shifter #(.shift("lr"), .width(15)) shifter_10 (
    .in(shifter_9_out[15:1]), .\dist ({3'b000, LAST_ADDR[0]}),
    .out({shifter_10_out_2, shifter_10_out, shifter_10_out_3[0]}));
  and and_12 (B9_ERR, shifter_10_out_3[0], shifter_10_out[0], shifter_10_out[1]);
  not not_18 (LAST_ADDR[1], shifter_10_out[0]);
  Shifter #(.shift("lr"), .width(14)) shifter_11 (
    .in({shifter_10_out_2, shifter_10_out}), .\dist ({3'b000, not_15_out[0]}),
    .out({shifter_11_out_2, shifter_11_out, shifter_11_out_3[0]}));
  and and_13 (BA_ERR, ~shifter_11_out_3[0], ~shifter_11_out[0], ~shifter_11_out[1]);  // AND_Gate
  not not_19 (LAST_ADDR[2], shifter_11_out[0]);
  Shifter #(.shift("lr"), .width(13)) shifter_12 (
    .in({shifter_11_out_2, shifter_11_out}), .\dist ({3'b000, LAST_ADDR[2]}),
    .out({shifter_12_out_2, shifter_12_out, shifter_12_out_3[0]}));
  and and_14 (BB_ERR, shifter_12_out_3[0], shifter_12_out[0], shifter_12_out[1]);
  not not_20 (LAST_ADDR[3], shifter_12_out[0]);
  Shifter #(.shift("lr"), .width(12)) shifter_13 (
    .in({shifter_12_out_2, shifter_12_out}), .\dist ({3'b000, not_16_out[0]}), .out(shifter_13_out));
  and and_15 (I29, ~out_3[31], ~out_3[30], ~out_3[29]);  // AND_Gate
  and and_16 (I28, ~out_3[30], ~out_3[29], ~out_3[28]);  // AND_Gate
  and and_17 (I27, ~out_3[29], ~out_3[28], ~out_3[27]);  // AND_Gate
  and and_18 (I26, ~out_3[28], ~out_3[27], ~out_3[26]);  // AND_Gate
  and and_19 (I24, ~out_3[26], ~out_3[25], ~out_3[24]);  // AND_Gate
  and and_20 (I23, ~out_3[25], ~out_3[24], ~out_3[23]);  // AND_Gate
  and and_21 (I25, ~out_3[27], ~out_3[26], ~out_3[25]);  // AND_Gate
  or or_1 (LAST_FE, out_4[1], B0_ERR, B1_ERR, B2_ERR, B3_ERR, B4_ERR, B5_ERR, B6_ERR, B7_ERR, B8_ERR, B9_ERR, BA_ERR, BB_ERR);
  and and_22 (I22, ~out_3[24], ~out_3[23], ~out_3[22]);  // AND_Gate
  and and_23 (I21, ~out_3[23], ~out_3[22], ~out_3[21]);  // AND_Gate
  and and_24 (I20, ~out_3[22], ~out_3[21], ~out_3[20]);  // AND_Gate
  and and_25 (I19, ~out_3[21], ~out_3[20], ~out_3[19]);  // AND_Gate
  and and_26 (I18, ~out_3[20], ~out_3[19], ~out_3[18]);  // AND_Gate
  and and_27 (I17, ~out_3[19], ~out_3[18], ~out_3[17]);  // AND_Gate
  and and_28 (I16, ~out_3[18], ~out_3[17], ~out_3[16]);  // AND_Gate
  and and_29 (I15, ~out_3[17], ~out_3[16], ~out_3[15]);  // AND_Gate
  and and_30 (I14, ~out_3[16], ~out_3[15], ~out_3[14]);  // AND_Gate
  and and_31 (I13, ~out_3[15], ~out_3[14], ~out_3[13]);  // AND_Gate
  and and_32 (I12, ~out_3[14], ~out_3[13], ~out_3[12]);  // AND_Gate
  and and_33 (I11, ~out_3[13], ~out_3[12], ~out_3[11]);  // AND_Gate
  and and_34 (I10, ~out_3[12], ~out_3[11], ~out_3[10]);  // AND_Gate
  and and_35 (I9, ~out_3[11], ~out_3[10], ~out_3[9]);  // AND_Gate
  and and_36 (I8, ~out_3[10], ~out_3[9], ~out_3[8]);  // AND_Gate
  and and_37 (I7, ~out_3[9], ~out_3[8], ~out_3[7]);  // AND_Gate
  and and_38 (I6, ~out_3[8], ~out_3[7], ~out_3[6]);  // AND_Gate
  and and_39 (I5, ~out_3[7], ~out_3[6], ~out_3[5]);  // AND_Gate
  and and_40 (I4, ~out_3[6], ~out_3[5], ~out_3[4]);  // AND_Gate
  Priority_Encoder #(.select(5)) priority_encoder_1 (
    .in0(I29), .in1(I28), .in2(I27), .in3(I26), .in4(I25), .in5(I24), .in6(I23), .in7(I22), .in8(I21),
    .in9(I20), .in10(I19), .in11(I18), .in12(I17), .in13(I16), .in14(I15), .in15(I14), .in16(I13),
    .in17(I12), .in18(I11), .in19(I10), .in20(I9), .in21(I8), .in22(I7), .in23(I6), .in24(I5), .in25(I4),
    .in26(1'b0), .in27(1'b0), .in28(1'b0), .in29(1'b0), .in30(1'b0), .in31(1'b0),
    .out(priority_encoder_1_out), .gs(FOUND_IDLE));  // open: en_out, en_in
  Subtractor #(.width(6)) subtractor_2 (
    .a(6'b011010), .b({1'b0, priority_encoder_1_out}), .out(subtractor_2_out));  // open: bin, bout
  Multiplexer #(.width(5)) multiplexer_1 (
    .in0({5{1'b0}}), .in1(subtractor_2_out[4:0]), .out(FRAME_LENGTH), .sel(FOUND_IDLE));

  // Other names for the same wires on the sheet: LAST_FRAME[24:0] = out_4; HIST[31:0] = out_3; B8 = LAST_ADDR[0];
  //   B9 = LAST_ADDR[1]; BA = LAST_ADDR[2]; BB = LAST_ADDR[3]; B0 = LAST_DATA[0]; B1 = LAST_DATA[1];
  //   B2 = LAST_DATA[2]; B3 = LAST_DATA[3]; B4 = LAST_DATA[4]; B5 = LAST_DATA[5]; B6 = LAST_DATA[6];
  //   B7 = LAST_DATA[7]; EOF_ERR = out_4[1]
endmodule

module TXRXD (
  input  DOUT,
  input  RXIN,
  output TXOUT,
  output DIN
);

  assign TXOUT = DOUT ? ~DOUT : 1'bz;  // Controlled_Inverter controlled_inverter_1
  not not_1 (DIN, RXIN);

  // Notes on the sheet:
  //   TXOUT: pull=down
endmodule

module VPWBController (
  input  CS,
  input  W,
  input  SER_IN,
  input  O,
  input  ADDR,
  input  [11:0] DATAIN,
  input  CLK,
  output SER_OUT,
  output I,
  output [11:0] DATAOUT
);

  wire and_1_out, and_2_out, and_3_out, and_4_out, and_5_out, and_6_out, DR, DRIE, ENA, IRQ_LEVEL, TBNF,
       TBNFIE, TXI, TXIIE, vpwbrx_1_empty, vpwbtx_1_full;
  wire [3:0] A, C;
  wire [11:0] vpwbrx_1_frame_out;

  Multiplexer #(.width(12)) multiplexer_1 (
    .in0({C, A, TXI, TBNF, DR, ENA}), .in1(vpwbrx_1_frame_out), .out(DATAOUT), .sel(ADDR));
  and and_1 (and_1_out, ~CS, ~W, ~ADDR);  // AND_Gate
  and and_2 (and_2_out, ~CS, ~W, ADDR);  // AND_Gate
  not not_1 (TBNF, vpwbtx_1_full);
  and and_3 (and_3_out, ~CS, ~O, ADDR);  // AND_Gate
  not not_2 (DR, vpwbrx_1_empty);
  Register #(.width(12)) register_1 (
    .D(DATAIN), .en(and_1_out), .Q({C, A, TXIIE, TBNFIE, DRIE, ENA}));  // open: clk, clr
  VPWBTX vpwbtx_1 (
    .FRAME_IN(DATAIN), .WRITE(and_2_out), .ENA(ENA), .CLK(CLK), .SER_IN(SER_IN), .FULL(vpwbtx_1_full),
    .IDLE(TXI), .SER_OUT(SER_OUT));
  VPWBRX vpwbrx_1 (
    .READ(and_3_out), .ENA(ENA), .CARE(C), .CLK(CLK), .ADDR(A), .SER_IN(SER_IN),
    .FRAME_OUT(vpwbrx_1_frame_out), .EMPTY(vpwbrx_1_empty));  // open: FULL
  and and_4 (and_4_out, DR, DRIE);
  and and_5 (and_5_out, TBNF, TBNFIE);
  and and_6 (and_6_out, TXI, TXIIE);
  not not_3 (I, IRQ_LEVEL);
  or or_1 (IRQ_LEVEL, and_4_out, and_5_out, and_6_out);

  // Other names for the same wires on the sheet: INT = I
endmodule

module VPWBTX (
  input  [11:0] FRAME_IN,
  input  SER_IN,
  input  WRITE,
  input  ENA,
  input  CLK,
  output SER_OUT,
  output FULL,
  output IDLE
);

  wire and_1_out, ENQUEUE, LOAD, or_1_out, QEMPTY, SROEMPTY, vpwbarbiter_1_arbl, vpwbarbiter_1_bitcmp,
       vpwbsro_1_ser_out;
  wire [3:0] vpwbsro_1_bitsleft;
  wire [11:0] vpwbframequeue_1_frame_out;

  VPWBFrameQueue vpwbframequeue_1 (
    .FRAME_IN(FRAME_IN), .ENQUEUE(ENQUEUE), .ENA(ENA), .CLK(CLK), .DEQUEUE(LOAD), .FULL(FULL),
    .FRAME_OUT(vpwbframequeue_1_frame_out), .EMPTY(QEMPTY));
  VPWBSRO vpwbsro_1 (
    .LOAD(LOAD), .ENA(ENA), .PARA_IN(vpwbframequeue_1_frame_out), .CLK(CLK), .SHIFT(vpwbarbiter_1_bitcmp),
    .RELOAD(vpwbarbiter_1_arbl), .EMPTY(SROEMPTY), .SER_OUT(vpwbsro_1_ser_out), .BITSLEFT(vpwbsro_1_bitsleft));
  or or_1 (or_1_out, vpwbsro_1_bitsleft[0], vpwbsro_1_bitsleft[1], vpwbsro_1_bitsleft[2], vpwbsro_1_bitsleft[3]);
  and and_1 (and_1_out, vpwbarbiter_1_bitcmp, or_1_out);
  and and_2 (ENQUEUE, ~FULL, WRITE);  // AND_Gate
  and and_3 (LOAD, ~QEMPTY, SROEMPTY);  // AND_Gate
  and and_4 (IDLE, QEMPTY, SROEMPTY);
  VPWBArbiter vpwbarbiter_1 (
    .DW(and_1_out), .EVENBIT(vpwbsro_1_bitsleft[0]), .DOUT(vpwbsro_1_ser_out), .ENA(ENA), .CLK(CLK),
    .RX(SER_IN), .ARBL(vpwbarbiter_1_arbl), .BITCMP(vpwbarbiter_1_bitcmp), .TX(SER_OUT));
endmodule

module VPWBRX (
  input  [3:0] CARE,
  input  [3:0] ADDR,
  input  SER_IN,
  input  READ,
  input  ENA,
  input  CLK,
  output [11:0] FRAME_OUT,
  output FULL,
  output EMPTY
);

  wire ADDR_MATCH, and_4_out, DROP, ENQUEUE, PASS, vpwbobserver_1_din, vpwbobserver_1_idle,
       vpwbobserver_1_newbit, vpwbsri_1_full;
  wire [3:0] ADDR_REG_MASKED, ADDR_RX, ADDR_RX_MASKED;
  wire [7:0] DATA_RX;

  and and_1 (ENQUEUE, vpwbsri_1_full, ~FULL);  // AND_Gate
  and and_2 (PASS, vpwbsri_1_full, ADDR_MATCH);
  and and_3 (DROP, vpwbsri_1_full, ~ADDR_MATCH);  // AND_Gate
  VPWBSRI vpwbsri_1 (
    .READ(ENQUEUE), .ENA(ENA), .CLK(CLK), .SER_IN(vpwbobserver_1_din), .NEWBIT(vpwbobserver_1_newbit),
    .CLEAR(vpwbobserver_1_idle), .FULL(vpwbsri_1_full), .PARA_OUT({DATA_RX, ADDR_RX}));
  VPWBFrameQueue vpwbframequeue_1 (
    .FRAME_IN({DATA_RX, ADDR_RX}), .ENQUEUE(ENQUEUE), .ENA(ENA), .CLK(CLK), .DEQUEUE(and_4_out), .FULL(FULL),
    .FRAME_OUT(FRAME_OUT), .EMPTY(EMPTY));
  and and_4 (and_4_out, READ, ~EMPTY);  // AND_Gate
  VPWBObserver vpwbobserver_1 (
    .ENA(ENA), .CLK(CLK), .RX(SER_IN), .DIN(vpwbobserver_1_din), .NEWBIT(vpwbobserver_1_newbit),
    .IDLE(vpwbobserver_1_idle));
  Comparator #(.width(4)) comparator_1 (.a(ADDR_RX_MASKED), .b(ADDR_REG_MASKED), .eq(ADDR_MATCH));  // open: gt, lt
  assign ADDR_RX_MASKED = ADDR_RX & CARE;  // AND_Gate and_5, 4 bits wide
  assign ADDR_REG_MASKED = ADDR & CARE;  // AND_Gate and_6, 4 bits wide
endmodule

module VPWBFrameQueue (
  input  [11:0] FRAME_IN,
  input  ENQUEUE,
  input  DEQUEUE,
  input  ENA,
  input  CLK,
  output [11:0] FRAME_OUT,
  output FULL,
  output EMPTY
);

  wire do_deq, do_enq, xor_1_out;
  wire [1:0] count;
  wire [11:0] register_1_q, register_2_q, register_3_q, register_4_q;

  and and_1 (do_enq, ENA, ENQUEUE, ~FULL);  // AND_Gate
  and and_2 (do_deq, ENA, DEQUEUE, ~EMPTY);  // AND_Gate
  Register #(.width(12)) register_1 (.D(FRAME_IN), .en(do_enq), .clk(CLK), .Q(register_1_q), .clr(1'b0));
  Register #(.width(12)) register_2 (.D(register_1_q), .en(do_enq), .clk(CLK), .Q(register_2_q), .clr(1'b0));
  Register #(.width(12)) register_3 (.D(register_2_q), .en(do_enq), .clk(CLK), .Q(register_3_q), .clr(1'b0));
  Register #(.width(12)) register_4 (.D(register_3_q), .en(do_enq), .clk(CLK), .Q(register_4_q), .clr(1'b0));
  nand nand_1 (EMPTY, count[0], count[1]);
  and and_3 (FULL, count[0], count[1]);
  xor xor_1 (xor_1_out, do_deq, do_enq);
  Counter #(.max('h3), .width(2)) counter_1 (
    .load(EMPTY), .D(2'b00), .count(xor_1_out), .Q(count), .up(do_enq), .clk(CLK));  // open: carry, clr
  Multiplexer #(.select(2), .width(12)) multiplexer_1 (
    .in0(register_1_q), .in1(register_2_q), .in2(register_3_q), .in3(register_4_q), .out(FRAME_OUT),
    .sel(count));
endmodule

module VPWBSRI (
  input  READ,
  input  SER_IN,
  input  NEWBIT,
  input  CLEAR,
  input  ENA,
  input  CLK,
  output FULL,
  output [11:0] PARA_OUT
);

  wire comparator_1_eq, not_1_out, not_2_out, not_3_out, not_4_out, not_5_out, or_1_out;
  wire [11:0] register_1_q;
  wire [12:0] fullShift;

  Comparator #(.width(13)) comparator_1 (.a(fullShift), .b({13{1'b0}}), .eq(comparator_1_eq));  // open: gt, lt
  Shift_Register #(.length(13)) shift_register_1 (
    .shift(NEWBIT), .in(SER_IN), .clk(CLK), .out(fullShift[12]), .load(comparator_1_eq), .clr(not_1_out),
    .d0(1'b1), .q0(fullShift[0]), .d1(1'b0), .q1(fullShift[1]), .d2(1'b0), .q2(fullShift[2]), .d3(1'b0),
    .q3(fullShift[3]), .d4(1'b0), .q4(fullShift[4]), .d5(1'b0), .q5(fullShift[5]), .d6(1'b0),
    .q6(fullShift[6]), .d7(1'b0), .q7(fullShift[7]), .d8(1'b0), .q8(fullShift[8]), .d9(1'b0),
    .q9(fullShift[9]), .d10(1'b0), .q10(fullShift[10]), .d11(1'b0), .q11(fullShift[11]), .d12(1'b0));  // open: q12
  not not_1 (not_1_out, CLK);
  not not_2 (not_2_out, CLK);
  Register #(.width(12)) register_1 (
    .D(fullShift[11:0]), .en(fullShift[12]), .clk(not_2_out), .Q(register_1_q), .clr(not_3_out));
  not not_3 (not_3_out, CLK);
  Multiplexer #(.width(12)) multiplexer_1 (.in0({12{1'b0}}), .in1(register_1_q), .out(PARA_OUT), .sel(READ));
  Register #(.width(1)) register_2 (.D(fullShift[12]), .clk(not_4_out), .Q(FULL), .clr(or_1_out));  // open: en
  not not_4 (not_4_out, CLK);
  or or_1 (or_1_out, not_5_out, READ);
  not not_5 (not_5_out, CLK);

  assign ENA = CLK;

  // Other names for the same wires on the sheet: shiftReg = fullShift[12]; regValue[11:0] = fullShift[11:0]
endmodule

module VPWBSRO (
  input  [11:0] PARA_IN,
  input  LOAD,
  input  SHIFT,
  input  RELOAD,
  input  ENA,
  input  CLK,
  output SER_OUT,
  output EMPTY,
  output [3:0] BITSLEFT
);

  wire and_1_out, and_2_out, not_1_out, not_2_out, or_1_out;

  or or_1 (or_1_out, RELOAD, LOAD);
  Shift_Register #(.length(13)) shift_register_1 (
    .shift(SHIFT), .in(1'b0), .clk(and_1_out), .out(SER_OUT), .clr(not_1_out), .d0(1'b1), .d1(PARA_IN[0]),
    .d2(PARA_IN[1]), .d3(PARA_IN[2]), .d4(PARA_IN[3]), .d5(PARA_IN[4]), .d6(PARA_IN[5]), .d7(PARA_IN[6]),
    .d8(PARA_IN[7]), .d9(PARA_IN[8]), .d10(PARA_IN[9]), .d11(PARA_IN[10]), .d12(PARA_IN[11]));  // open: load, q0, q1, q2, q3, q4, q5, q6, q7, q8, q9, q10, q11, q12
  and and_1 (and_1_out, CLK, ENA);
  not not_1 (not_1_out, ENA);
  not not_2 (not_2_out, ENA);
  and and_2 (and_2_out, CLK, ENA);
  Counter #(.max('hd), .ongoal("stay"), .width(4)) counter_1 (
    .load(or_1_out), .D(4'b1101), .count(SHIFT), .Q(BITSLEFT), .carry(EMPTY), .up(1'b0), .clk(and_2_out),
    .clr(not_2_out));

  // Notes on the sheet:
  //   PARA_IN: initial=0xa5f
endmodule

module VPWBArbiter (
  input  EVENBIT,
  input  DOUT,
  input  DW,
  input  RX,
  input  ENA,
  input  CLK,
  output TX,
  output ARBL,
  output BITCMP
);

  wire and_1_out, and_2_out, and_3_out, and_6_out, and_7_out, and_8_out, and_9_out, and_10_out, and_11_out,
       and_12_out, BIT1, BIT2, BUSIDLE, IDLE, NENA, not_1_out, not_2_out, not_4_out, not_5_out, not_6_out,
       not_7_out, not_8_out, not_9_out, not_10_out, or_2_out, or_3_out, or_4_out, register_1_q, register_2_q,
       SHORT, xor_1_out;

  not not_1 (not_1_out, ARBL);
  not not_2 (not_2_out, ARBL);
  and and_1 (and_1_out, BIT1, SHORT, not_1_out);
  and and_2 (and_2_out, BIT2, not_2_out);
  and and_3 (and_3_out, IDLE, BUSIDLE);
  not not_3 (NENA, ENA);
  or or_1 (BITCMP, and_1_out, and_2_out, and_3_out);
  Register #(.width(1)) register_1 (.D(DOUT), .en(DW), .clk(CLK), .Q(register_1_q), .clr(NENA));
  Register #(.width(1)) register_2 (.D(EVENBIT), .en(DW), .clk(CLK), .Q(register_2_q), .clr(NENA));
  not not_4 (not_4_out, IDLE);
  and and_4 (ARBL, not_4_out, xor_1_out);
  xor xor_1 (xor_1_out, TX, RX);
  xnor xnor_1 (SHORT, register_1_q, register_2_q);
  not not_5 (not_5_out, IDLE);
  and and_5 (TX, not_5_out, register_2_q);
  and and_6 (and_6_out, SHORT, BIT1);
  or or_2 (or_2_out, and_6_out, IDLE, BIT2);
  and and_7 (and_7_out, IDLE, BUSIDLE, DW);
  and and_8 (and_8_out, BIT1, SHORT, DW);
  and and_9 (and_9_out, BIT2, DW);
  not not_6 (not_6_out, DW);
  or or_3 (or_3_out, and_7_out, and_8_out, and_9_out);
  not not_7 (not_7_out, ARBL);
  not not_8 (not_8_out, ARBL);
  and and_10 (and_10_out, or_2_out, not_6_out);
  or or_4 (or_4_out, and_10_out, ARBL);
  and and_11 (and_11_out, or_3_out, not_7_out);
  not not_9 (not_9_out, SHORT);
  VPWBObserver vpwbobserver_1 (.ENA(ENA), .CLK(CLK), .RX(RX), .IDLE(BUSIDLE));  // open: DIN, NEWBIT
  not not_10 (not_10_out, or_4_out);
  D_Flip_Flop d_ff_1 (.D(and_11_out), .clk(CLK), .Q(BIT1), .reset(NENA));  // open: Qn, preset
  D_Flip_Flop d_ff_2 (.D(and_12_out), .clk(CLK), .Q(BIT2), .reset(NENA));  // open: Qn, preset
  and and_12 (and_12_out, BIT1, not_9_out, not_8_out);
  D_Flip_Flop d_ff_3 (.D(not_10_out), .clk(CLK), .Qn(IDLE), .reset(NENA));  // open: Q, preset
endmodule

module VPWBObserver (
  input  RX,
  input  ENA,
  input  CLK,
  output IDLE,
  output DIN,
  output NEWBIT
);

  wire and_1_out, and_2_out, ERR, NENA, not_2_out, not_3_out, not_4_out, or_2_out, PREV_IDLE, RX1, RX2, RX3,
       xnor_1_out, xor_1_out;

  not not_1 (NENA, ENA);
  nor nor_1 (PREV_IDLE, RX, RX1, RX2);
  not not_2 (not_2_out, IDLE);
  xnor xnor_1 (xnor_1_out, RX1, RX2);
  nor nor_2 (IDLE, RX, RX1, RX2);
  and and_1 (and_1_out, ERR, not_2_out);
  and and_2 (and_2_out, RX, RX1, RX2);
  or or_1 (DIN, RX1, xnor_1_out);
  or or_2 (or_2_out, and_1_out, and_2_out);
  D_Flip_Flop d_ff_1 (.D(or_2_out), .clk(CLK), .Q(ERR), .reset(NENA));  // open: Qn, preset
  xor xor_1 (xor_1_out, RX, RX1);
  not not_3 (not_3_out, ERR);
  and and_3 (NEWBIT, xor_1_out, not_3_out, not_4_out);
  not not_4 (not_4_out, PREV_IDLE);
  D_Flip_Flop d_ff_2 (.D(RX), .clk(CLK), .Q(RX1), .reset(NENA));  // open: Qn, preset
  D_Flip_Flop d_ff_3 (.D(RX1), .clk(CLK), .Q(RX2), .reset(NENA));  // open: Qn, preset
  D_Flip_Flop d_ff_4 (.D(RX2), .clk(CLK), .Q(RX3), .reset(NENA));  // open: Qn, preset
endmodule

module ObserverTest (
);

  wire and_1_out, CLK, DIN, IDLE, NEWBIT, NEWCHAR, PREVIDLE, RX;
  wire [4:0] counter_1_q;
  wire [6:0] CHAR_IN;

  Clock clock_1 (.out(CLK));
  D_Flip_Flop d_ff_1 (.D(IDLE), .clk(CLK), .Q(PREVIDLE));  // open: Qn, preset, reset
  and and_1 (and_1_out, IDLE, ~PREVIDLE);  // AND_Gate
  or or_1 (NEWCHAR, and_1_out, NEWBIT);
  TTY tty_1 (.data(CHAR_IN), .clk(CLK), .we(NEWCHAR));  // open: clr
  Multiplexer #(.select(2), .width(7)) multiplexer_1 (
    .in0(7'b0110000), .in1(7'b0110001), .in2(7'b1001001), .in3(7'b1001001), .out(CHAR_IN), .sel({IDLE, DIN}));
  VPWBObserver vpwbobserver_1 (.ENA(1'b1), .CLK(CLK), .RX(RX), .DIN(DIN), .NEWBIT(NEWBIT), .IDLE(IDLE));
  ROM #(.addrWidth(5), .dataWidth(1)) rom_1 (.addr(counter_1_q), .data(RX));
  Counter #(.max('h1f), .width(5)) counter_1 (
    .count(1'b1), .Q(counter_1_q), .clk(CLK));  // open: load, D, carry, up, clr

  // Notes on the sheet:
  //   contents of rom_1 (hex, n*v repeats v):
  //   0 0 1 0 1 1 0 0 1 0 1 1 0 1 0 0 1 1 0 0 1 1 1 0 1 0 0 1
endmodule

module TXRXTest (
  input  [11:0] in_1,
  input  in_2,
  input  in_3
);

  wire CLK, txrxd_1_din, txrxd_1_txout, vpwbmonitor_1_last_fe, vpwbtx_1_full, vpwbtx_1_idle, vpwbtx_1_ser_out;
  wire [3:0] vpwbmonitor_1_last_addr;
  wire [7:0] vpwbmonitor_1_last_data;
  wire [24:0] vpwbmonitor_1_out_4;
  wire [31:0] vpwbmonitor_1_out_3;

  Clock clock_1 (.out(CLK));
  // Probe on vpwbtx_1_full
  // Probe on vpwbtx_1_idle
  VPWBTX vpwbtx_1 (
    .FRAME_IN(in_1), .WRITE(in_2), .ENA(in_3), .CLK(CLK), .SER_IN(txrxd_1_din), .FULL(vpwbtx_1_full),
    .IDLE(vpwbtx_1_idle), .SER_OUT(vpwbtx_1_ser_out));
  TXRXD txrxd_1 (.DOUT(vpwbtx_1_ser_out), .RXIN(txrxd_1_txout), .DIN(txrxd_1_din), .TXOUT(txrxd_1_txout));
  Pull_Resistor #(.pull(1)) pull_resistor_1 (.node(txrxd_1_txout));
  // Probe on vpwbmonitor_1_out_3
  VPWBMonitor vpwbmonitor_1 (
    .RXIN(txrxd_1_txout), .CLK(CLK), .LAST_FE(vpwbmonitor_1_last_fe), .LAST_ADDR(vpwbmonitor_1_last_addr),
    .LAST_DATA(vpwbmonitor_1_last_data), .out_3(vpwbmonitor_1_out_3), .out_4(vpwbmonitor_1_out_4));
  // Probe on vpwbmonitor_1_out_4
  // Probe on vpwbmonitor_1_last_fe
  // Probe on vpwbmonitor_1_last_addr
  // Probe on vpwbmonitor_1_last_data
endmodule

module ArbiterTest (
);

  wire and_1_out, BITCMP, CLK, not_1_out, SHIFT, shift_register_1_out, vpwbarbiter_1_tx;
  wire [3:0] counter_1_q;

  Clock clock_1 (.out(CLK));
  Shift_Register #(.length(13)) shift_register_1 (
    .shift(SHIFT), .in(1'b0), .clk(CLK), .out(shift_register_1_out));  // open: load, clr, d0, q0, d1, q1, d2, q2, d3, q3, d4, q4, d5, q5, d6, q6, d7, q7, d8, q8, d9, q9, d10, q10, d11, q11, d12, q12
  Counter #(.max('hd), .width(4)) counter_1 (
    .count(SHIFT), .Q(counter_1_q), .clk(CLK));  // open: load, D, carry, up, clr
  and and_1 (and_1_out, counter_1_q[0], ~counter_1_q[1], counter_1_q[2], counter_1_q[3]);  // AND_Gate
  not not_1 (not_1_out, counter_1_q[0]);
  and and_2 (SHIFT, BITCMP, ~and_1_out);  // AND_Gate
  VPWBArbiter vpwbarbiter_1 (
    .DW(SHIFT), .EVENBIT(not_1_out), .DOUT(shift_register_1_out), .ENA(1'b1), .CLK(CLK),
    .RX(vpwbarbiter_1_tx), .BITCMP(BITCMP), .TX(vpwbarbiter_1_tx));  // open: ARBL
  Shift_Register #(.length(24)) shift_register_2 (
    .shift(1'b1), .in(vpwbarbiter_1_tx), .clk(CLK));  // open: out, load, clr, d0, q0, d1, q1, d2, q2, d3, q3, d4, q4, d5, q5, d6, q6, d7, q7, d8, q8, d9, q9, d10, q10, d11, q11, d12, q12, d13, q13, d14, q14, d15, q15, d16, q16, d17, q17, d18, q18, d19, q19, d20, q20, d21, q21, d22, q22, d23, q23
endmodule
